# Fritzing sketch raspLed (saved by Fritzing 0.9.3b)
breadboards: 1

parts:
  Raspberry_Pi_1 = Raspberry Pi 3 [part_number=RPI-3-V1.2]
  LED1 = RGB LED (com. cathode, rgb) [package="5 mm [THT]"]
  R1 = Resistor [tolerance=±5% resistance=220 package="2010 [SMD]"]

nets:
  N1: Raspberry_Pi_1.GND, LED1.common_cathode
  N2: Raspberry_Pi_1.GIPO17, R1.Pin_1
  N3: LED1.blue_anode, R1.Pin_0

// code stored in the sketch: Untitled.ino
import RPi.GPIO as GPIO
import time GPIO.setmode(GPIO.BOARD) 
GPIO.setup(7, GPIO.OUT) 

while True:   
	GPIO.output(7, True)    
	time.sleep(1)    	
	PIO.output(7, False)    
	time.sleep(1)
